# Fritzing sketch Leonardo_test_circuit (saved by Fritzing 0.9.2b)

parts:
  Part1 = Arduino Leonardo (Rev3b)
  U1 = POT [package=alps_pot]
  S1 = Round Pushbutton

nets:
  N1: Part1.D2/SDA, S1.leg1
  N2: Part1.5V, U1.A
  N3: Part1.GND, U1.E, S1.leg0
  N4: Part1.A0, U1.S
